# Fritzing sketch Home_Control (saved by Fritzing 0.7.7b)
breadboards: 1

parts:
  Arduino1 = Arduino
  R1 = Resistor [tolerance=±5% resistance=220 package=THT]
  LED1 = LED - 5mm [color="Red (633nm)" package="5 mm [THT]"]
  R2 = Photocell (LDR) [package=THT]
  R3 = Resistor [tolerance=±5% resistance=220 package=THT]

nets:
  N1: Arduino1.D9, R3.Pin_0
  N2: Arduino1.+5V, R1.Pin_0
  N3: Arduino1.GND, Arduino1.A0, LED1.cathode
  N4: R1.Pin_1, R2.pin_0
  N5: LED1.anode, R3.Pin_1
