# Fritzing sketch Aansluitingen (saved by Fritzing 0.7.7b)
breadboards: 1

parts:
  Arduino1 = Arduino
  LED1 = LED - 3mm [color="Red (633nm)" package="3 mm [THT]"]
  LED2 = LED - 3mm [color="Red (633nm)" package="3 mm [THT]"]
  LED3 = LED - 3mm [color="Red (633nm)" package="3 mm [THT]"]
  LED4 = LED - 3mm [color="Red (633nm)" package="3 mm [THT]"]
  LED5 = LED - 3mm [color="Red (633nm)" package="3 mm [THT]"]
  R2 = Rotary Potentiometer (Small) [maximum_resistance=100kΩ]
  R3 = Resistor [tolerance=±5% resistance=220 package=THT]
  R4 = Resistor [tolerance=±5% resistance=220 package=THT]
  R5 = Resistor [tolerance=±5% resistance=220 package=THT]
  R6 = Resistor [tolerance=±5% resistance=220 package=THT]
  R7 = Resistor [tolerance=±5% resistance=220 package=THT]

nets:
  N1: Arduino1.D7, LED1.anode, R7.Pin_0
  N2: Arduino1.D6, R6.Pin_1
  N3: Arduino1.D5, LED3.anode, R5.Pin_0
  N4: Arduino1.D4, LED4.anode, R4.Pin_0
  N5: Arduino1.D3, LED5.anode, R3.Pin_0
  N6: Arduino1.+5V, R2.leg2
  N7: Arduino1.GND, LED1.cathode, LED2.cathode, LED3.cathode, LED4.cathode, LED5.cathode, R2.leg1
  N8: Arduino1.A0, R2.wiper
  N9: LED2.anode, R6.Pin_0
